# Fritzing sketch minimum (saved by Fritzing 1.0.5)

parts:
  U1 = ESP32-38PinWide [part_number=ESP32-38PinWide]
  A1 = TJA1050 CAN Module
  cntl1 = roboRIO
  Mod1 = VRM

nets:
  N1: U1.GND, A1.Pin_2, Mod1.5V_2A_GND0, Mod1.InGnd
  N2: U1.VIN, A1.Pin_3, Mod1.5V_2A_5V0
  N3: U1.GPIO4, A1.Pin_1
  N4: U1.GPIO5, A1.Pin_4
  N5: A1.Pin_5, cntl1.CAN_L_(GRN)
  N6: A1.Pin_6, cntl1.CAN_H_(YEL)

custom parts:
  ESP32-38PinWide: Generic 38-Pin ESP32 with wide format (only access to one side of pins on a breadboard) based on Stephen Lilley's HiLetgo ESP-WROOM-32 ESP32 ESP-32S Development Board.
  TJA1050 CAN Module: TJA1050 CAN module CAN bus module.
